// Logisim project Asiignment1try.circ as structural Verilog: 1 circuit, main circuit main
module main (
  input  Play,
  input  Pause,
  input  _1___Increase,
  input  in_4
);

  wire and_1_out, and_2_out, and_3_out, and_4_out, and_5_out, and_6_out, and_7_out, and_8_out, and_9_out,
       and_10_out, and_11_out, and_12_out, and_13_out, and_14_out, and_15_out, and_16_out, and_17_out,
       and_18_out, and_19_out, button_1_out, button_2_out, d_ff_1_q, d_ff_2_q, d_ff_3_q, d_ff_4_q, d_ff_5_q,
       d_ff_6_q, d_ff_7_q, d_ff_8_q, d_ff_9_q, j_k_ff_2_q, not_1_out, not_2_out, or_1_out, or_2_out,
       or_3_out, or_4_out, or_5_out, or_6_out, or_7_out, or_8_out, xor_1_out;
  wire [3:0] j_k_ff_1_q, j_k_ff_4_q;

  not not_1 (not_1_out, Play);
  Button button_1 (.out(button_1_out));
  or or_1 (or_1_out, and_1_out, and_2_out);
  and and_1 (and_1_out, _1___Increase, _1___Increase);
  and and_2 (and_2_out, d_ff_2_q, not_2_out);
  not not_2 (not_2_out, _1___Increase);
  xor xor_1 (xor_1_out, Pause, Play);
  and and_3 (and_3_out, Play, Pause);
  LED led_1 (.in(d_ff_1_q));
  D_Flip_Flop d_ff_1 (.D(or_1_out), .clk(button_1_out), .Q(d_ff_1_q), .reset(not_1_out));  // open: Qn, preset
  LED led_2 (.in(xor_1_out));
  LED led_3 (.in(and_3_out));
  LED led_4 (.in(d_ff_2_q));
  LED led_5 (.in(d_ff_3_q));
  D_Flip_Flop d_ff_2 (.D(or_2_out), .clk(button_1_out), .Q(d_ff_2_q), .reset(not_1_out));  // open: Qn, preset
  or or_2 (or_2_out, and_4_out, and_5_out);
  and and_4 (and_4_out, _1___Increase, d_ff_1_q);
  and and_5 (and_5_out, d_ff_3_q, not_2_out);
  Button button_2 (.out(button_2_out));
  LED led_6 (.in(d_ff_4_q));
  LED led_7 (.in(d_ff_5_q));
  and and_6 (and_6_out, _1___Increase, d_ff_2_q);
  and and_7 (and_7_out, d_ff_4_q, not_2_out);
  Hex_Digit_Display hex_digit_display_1 (.value(j_k_ff_4_q));  // open: dp
  LED led_8 (.in(d_ff_6_q));
  LED led_9 (.in(d_ff_7_q));
  D_Flip_Flop d_ff_3 (.D(or_3_out), .clk(button_1_out), .Q(d_ff_3_q), .reset(not_1_out));  // open: Qn, preset
  or or_3 (or_3_out, and_6_out, and_7_out);
  Hex_Digit_Display hex_digit_display_2 (.value(j_k_ff_1_q));  // open: dp
  LED led_10 (.in(d_ff_8_q));
  D_Flip_Flop d_ff_4 (.D(or_4_out), .clk(button_1_out), .Q(d_ff_4_q), .reset(not_1_out));  // open: Qn, preset
  or or_4 (or_4_out, and_8_out, and_9_out);
  and and_8 (and_8_out, _1___Increase, d_ff_3_q);
  and and_9 (and_9_out, d_ff_5_q, not_2_out);
  and and_10 (and_10_out, _1___Increase, d_ff_4_q);
  and and_11 (and_11_out, d_ff_6_q, not_2_out);
  D_Flip_Flop d_ff_5 (.D(or_5_out), .clk(button_1_out), .Q(d_ff_5_q), .reset(not_1_out));  // open: Qn, preset
  or or_5 (or_5_out, and_10_out, and_11_out);
  or or_6 (or_6_out, and_12_out, and_13_out);
  and and_12 (and_12_out, _1___Increase, d_ff_5_q);
  and and_13 (and_13_out, d_ff_7_q, not_2_out);
  D_Flip_Flop d_ff_6 (.D(or_6_out), .clk(button_1_out), .Q(d_ff_6_q), .reset(not_1_out));  // open: Qn, preset
  D_Flip_Flop d_ff_7 (.D(or_7_out), .clk(button_1_out), .Q(d_ff_7_q), .reset(not_1_out));  // open: Qn, preset
  or or_7 (or_7_out, and_14_out, and_15_out);
  and and_14 (and_14_out, _1___Increase, d_ff_6_q);
  and and_15 (and_15_out, d_ff_8_q, not_2_out);
  and and_16 (and_16_out, in_4, not_2_out);
  D_Flip_Flop d_ff_8 (.D(or_8_out), .clk(button_1_out), .Q(d_ff_8_q), .reset(not_1_out));  // open: Qn, preset
  or or_8 (or_8_out, and_17_out, and_16_out);
  and and_17 (and_17_out, _1___Increase, d_ff_7_q);
  J_K_Flip_Flop #(.trigger("falling")) j_k_ff_1 (
    .J(Play), .K(Play), .clk(button_2_out), .Q(j_k_ff_1_q[0]), .reset(and_18_out));  // open: Qn, preset
  D_Flip_Flop d_ff_9 (.D(j_k_ff_2_q), .clk(button_2_out), .Q(d_ff_9_q));  // open: Qn, preset, reset
  J_K_Flip_Flop j_k_ff_2 (
    .J(j_k_ff_1_q[3]), .K(j_k_ff_1_q[3]), .clk(button_2_out), .Q(j_k_ff_2_q));  // open: Qn, preset, reset
  J_K_Flip_Flop #(.trigger("falling")) j_k_ff_3 (
    .J(Play), .K(Play), .clk(j_k_ff_1_q[0]), .Q(j_k_ff_1_q[1]), .reset(and_18_out));  // open: Qn, preset
  J_K_Flip_Flop #(.trigger("falling")) j_k_ff_4 (
    .J(d_ff_9_q), .K(d_ff_9_q), .clk(button_2_out), .Q(j_k_ff_4_q[0]), .reset(and_19_out));  // open: Qn, preset
  J_K_Flip_Flop #(.trigger("falling")) j_k_ff_5 (
    .J(Play), .K(Play), .clk(j_k_ff_1_q[1]), .Q(j_k_ff_1_q[2]), .reset(and_18_out));  // open: Qn, preset
  J_K_Flip_Flop #(.trigger("falling")) j_k_ff_6 (
    .J(d_ff_9_q), .K(d_ff_9_q), .clk(j_k_ff_4_q[0]), .Q(j_k_ff_4_q[1]), .reset(and_19_out));  // open: Qn, preset
  J_K_Flip_Flop #(.trigger("falling")) j_k_ff_7 (
    .J(Play), .K(Play), .clk(j_k_ff_1_q[2]), .Q(j_k_ff_1_q[3]), .reset(and_18_out));  // open: Qn, preset
  J_K_Flip_Flop #(.trigger("falling")) j_k_ff_8 (
    .J(d_ff_9_q), .K(d_ff_9_q), .clk(j_k_ff_4_q[1]), .Q(j_k_ff_4_q[2]), .reset(and_19_out));  // open: Qn, preset
  and and_18 (and_18_out, j_k_ff_1_q[3], j_k_ff_1_q[1]);
  J_K_Flip_Flop #(.trigger("falling")) j_k_ff_9 (
    .J(d_ff_9_q), .K(d_ff_9_q), .clk(j_k_ff_4_q[2]), .Q(j_k_ff_4_q[3]), .reset(and_19_out));  // open: Qn, preset
  and and_19 (and_19_out, j_k_ff_4_q[3], j_k_ff_4_q[1]);

  // Notes on the sheet:
  //   Volume Control
  //   0 = Decrease
  //   Volume Toggle
  //   play
  //   Volume Level
  //   pause
endmodule
