// Logisim project Tracks.circ as structural Verilog: 1 circuit, main circuit main
module main (
  input  in_1,
  input  in_2
);

  wire and_1_out, clock_1_out;
  wire [2:0] j_k_ff_3_q;

  Clock clock_1 (.out(clock_1_out));
  J_K_Flip_Flop j_k_ff_1 (
    .J(and_1_out), .clk(clock_1_out), .K(and_1_out), .Q(j_k_ff_3_q[2]));  // open: Qn, preset, en, reset
  LED led_1 (.in(j_k_ff_3_q[2]));
  and and_1 (and_1_out, j_k_ff_3_q[0], j_k_ff_3_q[1]);
  J_K_Flip_Flop j_k_ff_2 (
    .J(j_k_ff_3_q[0]), .clk(clock_1_out), .K(j_k_ff_3_q[0]), .Q(j_k_ff_3_q[1]));  // open: Qn, preset, en, reset
  LED led_2 (.in(j_k_ff_3_q[1]));
  J_K_Flip_Flop j_k_ff_3 (.J(in_1), .clk(clock_1_out), .K(in_1), .Q(j_k_ff_3_q[0]));  // open: Qn, preset, en, reset
  Hex_Digit_Display hex_digit_display_1 (.value({in_2, j_k_ff_3_q}));  // open: dp
  LED led_3 (.in(j_k_ff_3_q[0]));

  // Notes on the sheet:
  //   Q3
  //   Q2
  //   Q1
endmodule
