// Logisim project Volume.circ as structural Verilog: 1 circuit, main circuit main
module main (
  input  in_1,
  input  in_2
);

  wire and_1_out, and_2_out, and_3_out, and_4_out, and_5_out, and_6_out, and_7_out, and_8_out, and_9_out,
       and_10_out, clock_1_out, d_ff_1_q, d_ff_2_q, d_ff_3_q, d_ff_4_q, d_ff_5_q, not_1_out, or_1_out,
       or_2_out, or_3_out, or_4_out, or_5_out;

  Clock clock_1 (.out(clock_1_out));
  and and_1 (and_1_out, d_ff_2_q, not_1_out);
  or or_1 (or_1_out, and_2_out, and_1_out);
  and and_2 (and_2_out, in_2, in_2);
  not not_1 (not_1_out, in_2);
  LED led_1 (.in(d_ff_1_q));
  D_Flip_Flop d_ff_1 (.clk(clock_1_out), .D(or_1_out), .Q(d_ff_1_q));  // open: Qn, preset, en, reset
  and and_3 (and_3_out, d_ff_3_q, not_1_out);
  or or_2 (or_2_out, and_4_out, and_3_out);
  and and_4 (and_4_out, in_2, d_ff_1_q);
  LED led_2 (.in(d_ff_2_q));
  D_Flip_Flop d_ff_2 (.clk(clock_1_out), .D(or_2_out), .Q(d_ff_2_q));  // open: Qn, preset, en, reset
  or or_3 (or_3_out, and_6_out, and_5_out);
  and and_5 (and_5_out, d_ff_4_q, not_1_out);
  D_Flip_Flop d_ff_3 (.clk(clock_1_out), .D(or_3_out), .Q(d_ff_3_q));  // open: Qn, preset, en, reset
  and and_6 (and_6_out, in_2, d_ff_2_q);
  LED led_3 (.in(d_ff_3_q));
  or or_4 (or_4_out, and_8_out, and_7_out);
  and and_7 (and_7_out, d_ff_5_q, not_1_out);
  LED led_4 (.in(d_ff_4_q));
  D_Flip_Flop d_ff_4 (.clk(clock_1_out), .D(or_4_out), .Q(d_ff_4_q));  // open: Qn, preset, en, reset
  and and_8 (and_8_out, in_2, d_ff_3_q);
  or or_5 (or_5_out, and_9_out, and_10_out);
  and and_9 (and_9_out, in_2, d_ff_4_q);
  and and_10 (and_10_out, in_1, not_1_out);
  LED led_5 (.in(d_ff_5_q));
  D_Flip_Flop d_ff_5 (.clk(clock_1_out), .D(or_5_out), .Q(d_ff_5_q));  // open: Qn, preset, en, reset

  // Notes on the sheet:
  //   Increase or Decrease
  //   1 = Increase
  //   0 = Decrease
endmodule
