// Logisim project pause-play.circ as structural Verilog: 1 circuit, main circuit main
module main (
  input  play,
  input  pause,
  output pause_2,
  output play_2
);

  xor xor_1 (pause_2, play, pause);
  and and_1 (play_2, pause, play);
endmodule
