// Logisim project task5.circ as structural Verilog: 1 circuit, main circuit main
module main (
  input  input_1,
  input  input_2,
  input  carry_in,
  output sum,
  output carry
);

  wire and_1_out, and_2_out, xor_1_out;

  xor xor_1 (xor_1_out, input_1, input_2);
  and and_1 (and_1_out, input_1, input_2);
  and and_2 (and_2_out, carry_in, xor_1_out);
  xor xor_2 (sum, xor_1_out, carry_in);
  or or_1 (carry, and_2_out, and_1_out);
endmodule
