// Logisim project TASK3.circ as structural Verilog: 1 circuit, main circuit main
module main (
  input  in_1
);

  wire a_out, and_1_out, and_2_out, b_out, clock_1_out, not_1_out;

  Clock clock_1 (.out(clock_1_out));
  not not_1 (not_1_out, in_1);
  and and_1 (and_1_out, clock_1_out, not_1_out);
  and and_2 (and_2_out, clock_1_out, in_1);
  nor a (a_out, and_1_out, b_out);
  nor b (b_out, a_out, and_2_out);
  LED led_1 (.in(a_out));
  LED led_2 (.in(b_out));

  // Notes on the sheet:
  //   SET
  //   RESET
  //   Q
  //   Q'
endmodule
