// Logisim project task2.circ as structural Verilog: 1 circuit, main circuit main
module main (
  input  set,
  input  reset
);

  wire a_out, b_out;

  nor a (a_out, set, b_out);
  nor b (b_out, a_out, reset);
  LED led_1 (.in(a_out));
  LED led_2 (.in(b_out));

  // Notes on the sheet:
  //   Q
  //   Q'
endmodule
