// Logisim project 3-bit-ripple.circ as structural Verilog: 1 circuit, main circuit main
module main (
  input  in_1,
  input  in_2
);

  wire clock_1_out, j_k_ff_1_q, j_k_ff_2_q, j_k_ff_3_q;

  Clock clock_1 (.out(clock_1_out));
  J_K_Flip_Flop j_k_ff_1 (.J(in_1), .clk(j_k_ff_2_q), .K(in_1), .Q(j_k_ff_1_q), .reset(in_2));  // open: Qn, preset, en
  LED led_1 (.in(j_k_ff_1_q));
  J_K_Flip_Flop j_k_ff_2 (.J(in_1), .clk(j_k_ff_3_q), .K(in_1), .Q(j_k_ff_2_q), .reset(in_2));  // open: Qn, preset, en
  LED led_2 (.in(j_k_ff_2_q));
  J_K_Flip_Flop j_k_ff_3 (.J(in_1), .clk(clock_1_out), .K(in_1), .Q(j_k_ff_3_q), .reset(in_2));  // open: Qn, preset, en
  LED led_3 (.in(j_k_ff_3_q));

  // Notes on the sheet:
  //   PULL TO RESET
  //   3-BIT RIPPLE (111 TO 000) RISING EDGE
  //   Q2
  //   Q1
  //   Q0
endmodule
