// Logisim project 4-bit-register.circ as structural Verilog: 1 circuit, main circuit main
module main (
  input  in_1,
  input  in_2,
  input  in_3,
  input  in_4,
  input  in_5
);

  wire clock_1_out, d_ff_1_q, d_ff_2_q, d_ff_3_q, d_ff_4_q;

  Clock clock_1 (.out(clock_1_out));
  D_Flip_Flop d_ff_1 (.clk(clock_1_out), .D(in_1), .Q(d_ff_1_q), .reset(in_5));  // open: Qn, preset, en
  LED led_1 (.in(d_ff_1_q));
  D_Flip_Flop d_ff_2 (.clk(clock_1_out), .D(in_2), .Q(d_ff_2_q), .reset(in_5));  // open: Qn, preset, en
  LED led_2 (.in(d_ff_2_q));
  D_Flip_Flop d_ff_3 (.clk(clock_1_out), .D(in_3), .Q(d_ff_3_q), .reset(in_5));  // open: Qn, preset, en
  LED led_3 (.in(d_ff_3_q));
  D_Flip_Flop d_ff_4 (.clk(clock_1_out), .D(in_4), .Q(d_ff_4_q), .reset(in_5));  // open: Qn, preset, en
  LED led_4 (.in(d_ff_4_q));

  // Notes on the sheet:
  //   PULL UP TO RESET
  //   INPUT
  //   CLOCK
  //   OUTPUT
endmodule
