// Logisim project mod6.circ as structural Verilog: 1 circuit, main circuit main
module main (
  input  in_1
);

  wire and_1_out, and_2_out, clock_1_out, j_k_ff_1_q, j_k_ff_2_q, j_k_ff_3_q;

  Clock clock_1 (.out(clock_1_out));
  J_K_Flip_Flop j_k_ff_1 (
    .J(and_1_out), .clk(clock_1_out), .K(and_1_out), .Q(j_k_ff_1_q), .reset(and_2_out));  // open: Qn, preset, en
  LED led_1 (.in(j_k_ff_1_q));
  and and_1 (and_1_out, j_k_ff_3_q, j_k_ff_2_q);
  J_K_Flip_Flop j_k_ff_2 (
    .J(j_k_ff_3_q), .clk(clock_1_out), .K(j_k_ff_3_q), .Q(j_k_ff_2_q), .reset(and_2_out));  // open: Qn, preset, en
  LED led_2 (.in(j_k_ff_2_q));
  J_K_Flip_Flop j_k_ff_3 (
    .J(in_1), .clk(clock_1_out), .K(in_1), .Q(j_k_ff_3_q), .reset(and_2_out));  // open: Qn, preset, en
  LED led_3 (.in(j_k_ff_3_q));
  and and_2 (and_2_out, j_k_ff_1_q, j_k_ff_2_q);

  // Notes on the sheet:
  //   Q3
  //   Q2
  //   Q1
endmodule
